// Logisim project 16_bit_adder.circ as structural Verilog: 1 circuit, main circuit main
module main (
  input  in_1,
  input  a0,
  input  a1,
  input  a2,
  input  a3,
  input  a4,
  input  a5,
  input  a6,
  input  a7,
  input  a0_2,
  input  a1_2,
  input  a2_2,
  input  a3_2,
  input  a4_2,
  input  a5_2,
  input  a6_2,
  input  a7_2,
  input  b0,
  input  b1,
  input  b2,
  input  b3,
  input  b4,
  input  b5,
  input  b6,
  input  b7,
  input  b0_2,
  input  b1_2,
  input  b2_2,
  input  b3_2,
  input  b4_2,
  input  b5_2,
  input  b6_2,
  input  b7_2,
  output _0,
  output _1,
  output _2,
  output _3,
  output _4,
  output _5,
  output _6,
  output _7,
  output _0_2,
  output _1_2,
  output _2_2,
  output _3_2,
  output _4_2,
  output _5_2,
  output _6_2,
  output _7_2,
  output out_50
);

  wire main_1_out_26;

  _8_bit_adder_main main_1 (
    .in_1(in_1), .a0(a0), .a1(a1), .a2(a2), .a3(a3), .a4(a4), .a5(a5), .a6(a6), .a7(a7), .b0(b0), .b1(b1),
    .b2(b2), .b3(b3), .b4(b4), .b5(b5), .b6(b6), .b7(b7), ._0(_0), ._1(_1), ._2(_2), ._3(_3), ._4(_4),
    ._5(_5), ._6(_6), ._7(_7), .out_26(main_1_out_26));
  _8_bit_adder_main main_2 (
    .in_1(main_1_out_26), .a0(a0_2), .a1(a1_2), .a2(a2_2), .a3(a3_2), .a4(a4_2), .a5(a5_2), .a6(a6_2),
    .a7(a7_2), .b0(b0_2), .b1(b1_2), .b2(b2_2), .b3(b3_2), .b4(b4_2), .b5(b5_2), .b6(b6_2), .b7(b7_2),
    ._0(_0_2), ._1(_1_2), ._2(_2_2), ._3(_3_2), ._4(_4_2), ._5(_5_2), ._6(_6_2), ._7(_7_2), .out_26(out_50));
endmodule
