// Logisim project 1_to_2_decoder.circ as structural Verilog: 1 circuit, main circuit main
module main (
  input  in_1,
  input  in_2,
  output out_3,
  output out_4
);

  wire not_1_out;

  not not_1 (not_1_out, in_1);
  and and_1 (out_3, not_1_out, in_2);
  and and_2 (out_4, in_1, in_2);
endmodule
