// Logisim project 2_to_4_decoder.circ as structural Verilog: 1 circuit, main circuit main
module main (
  input  in_1,
  input  in_2,
  input  in_3,
  output out_4,
  output out_5,
  output out_6,
  output out_7
);

  wire main_1_out_3, main_1_out_4, main_2_out_3, main_2_out_4, not_1_out;

  not not_1 (not_1_out, in_2);
  _1_to_2_decoder_main main_1 (.in_1(in_1), .in_2(not_1_out), .out_3(main_1_out_3), .out_4(main_1_out_4));
  _1_to_2_decoder_main main_2 (.in_1(in_1), .in_2(in_2), .out_3(main_2_out_3), .out_4(main_2_out_4));
  and and_1 (out_4, main_1_out_3, in_3);
  and and_2 (out_5, main_1_out_4, in_3);
  and and_3 (out_6, main_2_out_3, in_3);
  and and_4 (out_7, main_2_out_4, in_3);
endmodule
