// Logisim project 3_to_8_decoder.circ as structural Verilog: 1 circuit, main circuit main
module main (
  input  in_1,
  input  in_2,
  input  in_3,
  input  in_4,
  output out_5,
  output out_6,
  output out_7,
  output out_8,
  output out_9,
  output out_10,
  output out_11,
  output out_12
);

  wire main_1_out_4, main_1_out_5, main_1_out_6, main_1_out_7, main_2_out_4, main_2_out_5, main_2_out_6,
       main_2_out_7, not_1_out;

  not not_1 (not_1_out, in_3);
  _2_to_4_decoder_main main_1 (
    .in_1(in_1), .in_2(in_2), .in_3(not_1_out), .out_4(main_1_out_4), .out_5(main_1_out_5),
    .out_6(main_1_out_6), .out_7(main_1_out_7));
  _2_to_4_decoder_main main_2 (
    .in_1(in_1), .in_2(in_2), .in_3(in_3), .out_4(main_2_out_4), .out_5(main_2_out_5), .out_6(main_2_out_6),
    .out_7(main_2_out_7));
  and and_1 (out_5, main_1_out_4, in_4);
  and and_2 (out_6, main_1_out_5, in_4);
  and and_3 (out_7, main_1_out_6, in_4);
  and and_4 (out_8, main_1_out_7, in_4);
  and and_5 (out_9, main_2_out_4, in_4);
  and and_6 (out_10, main_2_out_5, in_4);
  and and_7 (out_11, main_2_out_6, in_4);
  and and_8 (out_12, main_2_out_7, in_4);
endmodule
