// Logisim project 4_to_2_multiplexer.circ as structural Verilog: 1 circuit, main circuit main
module main (
  input  in_1,
  input  in_2,
  input  in_3,
  input  in_4,
  input  in_5,
  input  in_6,
  output out_7
);

  wire main_1_out_4, main_2_out_4;

  _2_to_1_multiplexer_main main_1 (.in_1(in_1), .in_2(in_2), .in_3(in_5), .out_4(main_1_out_4));
  _2_to_1_multiplexer_main main_2 (.in_1(in_3), .in_2(in_4), .in_3(in_5), .out_4(main_2_out_4));
  _2_to_1_multiplexer_main main_3 (.in_1(main_1_out_4), .in_2(main_2_out_4), .in_3(in_6), .out_4(out_7));
endmodule
