// Logisim project 8_bit_adder.circ as structural Verilog: 1 circuit, main circuit main
module main (
  input  in_1,
  input  a0,
  input  a1,
  input  a2,
  input  a3,
  input  a4,
  input  a5,
  input  a6,
  input  a7,
  input  b0,
  input  b1,
  input  b2,
  input  b3,
  input  b4,
  input  b5,
  input  b6,
  input  b7,
  output _0,
  output _1,
  output _2,
  output _3,
  output _4,
  output _5,
  output _6,
  output _7,
  output out_26
);

  wire main_1_o, main_2_o, main_3_o, main_4_o, main_5_o, main_6_o, main_7_o;

  one_bit_adder_main main_1 (.i(in_1), .a(a0), .b(b0), .r(_0), .o(main_1_o));
  one_bit_adder_main main_2 (.i(main_1_o), .a(a1), .b(b1), .r(_1), .o(main_2_o));
  one_bit_adder_main main_3 (.i(main_2_o), .a(a2), .b(b2), .r(_2), .o(main_3_o));
  one_bit_adder_main main_4 (.i(main_3_o), .a(a3), .b(b3), .r(_3), .o(main_4_o));
  one_bit_adder_main main_5 (.i(main_4_o), .a(a4), .b(b4), .r(_4), .o(main_5_o));
  one_bit_adder_main main_6 (.i(main_5_o), .a(a5), .b(b5), .r(_5), .o(main_6_o));
  one_bit_adder_main main_7 (.i(main_6_o), .a(a6), .b(b6), .r(_6), .o(main_7_o));
  one_bit_adder_main main_8 (.i(main_7_o), .a(a7), .b(b7), .r(_7), .o(out_26));
endmodule
