// Logisim project 8_to_3_encoder.circ as structural Verilog: 1 circuit, main circuit main
module main (
  input  in_1,
  input  in_2,
  input  in_3,
  input  in_4,
  input  in_5,
  input  in_6,
  input  in_7,
  input  in_8,
  output out_9,
  output out_10,
  output out_11
);

  wire or_1_out, or_2_out, or_3_out, or_4_out, or_5_out;

  or or_1 (or_1_out, in_2, in_4);
  or or_2 (or_2_out, in_6, in_8);
  or or_3 (or_3_out, in_3, in_4);
  or or_4 (or_4_out, in_5, in_6);
  or or_5 (or_5_out, in_7, in_8);
  or or_6 (out_9, or_1_out, or_2_out);
  or or_7 (out_10, or_3_out, or_5_out);
  or or_8 (out_11, or_4_out, or_5_out);
endmodule
