// Logisim project 8_to_3_multiplexer.circ as structural Verilog: 1 circuit, main circuit main
module main (
  input  in_1,
  input  in_2,
  input  in_3,
  input  in_4,
  input  in_5,
  input  in_6,
  input  in_7,
  input  in_8,
  input  in_9,
  input  in_10,
  input  in_11,
  output out_12
);

  wire main_1_out_7, main_3_out_7;

  _4_to_2_multiplexer_main main_1 (
    .in_1(in_1), .in_2(in_2), .in_3(in_3), .in_4(in_4), .in_5(in_9), .in_6(in_10), .out_7(main_1_out_7));
  _2_to_1_multiplexer_main main_2 (.in_1(main_1_out_7), .in_2(main_3_out_7), .in_3(in_11), .out_4(out_12));
  _4_to_2_multiplexer_main main_3 (
    .in_1(in_5), .in_2(in_6), .in_3(in_7), .in_4(in_8), .in_5(in_9), .in_6(in_10), .out_7(main_3_out_7));
endmodule
