// Logisim project one_bit_adder.circ as structural Verilog: 1 circuit, main circuit main
module main (
  input  i,
  input  a,
  input  b,
  output r,
  output o
);

  wire a_b_out, a_b_prime_out, a_prime_b_out, a_prime_b_prime_out, and_1_out, and_2_out, and_3_out,
       not_1_out, not_2_out, not_3_out, or_1_out, or_2_out;

  not not_1 (not_1_out, i);
  not not_2 (not_2_out, a);
  not not_3 (not_3_out, b);
  and a_b (a_b_out, a, b);
  and a_prime_b (a_prime_b_out, not_2_out, b);
  and a_b_prime (a_b_prime_out, a, not_3_out);
  and a_prime_b_prime (a_prime_b_prime_out, not_2_out, not_3_out);
  or or_1 (or_1_out, a_prime_b_out, a_b_prime_out);
  or or_2 (or_2_out, a_b_out, a_prime_b_prime_out);
  and and_1 (and_1_out, i, or_2_out);
  and and_2 (and_2_out, not_1_out, or_1_out);
  and and_3 (and_3_out, or_1_out, i);
  or or_3 (r, and_1_out, and_2_out);
  or or_4 (o, and_3_out, a_b_out);
endmodule
